# Fritzing sketch Telemetrie station fritzing (saved by Fritzing 0.9.3b)

parts:
  Part1 = Arduino Uno (Rev3)
  GY1 = MPU-6050 Board GY-521 [form="♀ (female)" package=THT]
  JP1 = Header 4 [package=jst-4-pth]

nets:
  N1: Part1.A4/SDA, GY1.pin4
  N2: Part1.A5/SCL, GY1.pin3
  N3: Part1.D11_PWM/MOSI, JP1.2
  N4: Part1.D12/MISO, JP1.1
  N5: Part1.5V, GY1.pin1, JP1.4
  N6: Part1.GND, GY1.pin2, JP1.3

notes:
  VCC GND TRIG ECHO

custom parts:
  MPU-6050 Board GY-521: Acelerometro y Giroscopio MPU-6050 Board GY-521
